# Fritzing sketch Spooky Eyes_with_sensor (saved by Fritzing 0.9.3b)

parts:
  Part1 = Arduino Uno (Rev3)
  NEOPIXEL1 = Neopixel Strip -- Black (30/m)
  Part2 = SRF05 Ultrasonic Rangefinder
  Power_plug1 = Power plug  # not connected
  NEOPIXEL2 = Neopixel Strip -- Black (30/m)
  NEOPIXEL3 = Neopixel Strip -- Black (30/m)
  NEOPIXEL4 = Neopixel Strip -- Black (30/m)
  NEOPIXEL5 = Neopixel Strip -- Black (30/m)

nets:
  N1: Part1.D8, Part2.Trig
  N2: Part1.D6_PWM, NEOPIXEL1.Dout
  N3: Part1.D7, Part2.Echo
  N4: NEOPIXEL1.GND#1, NEOPIXEL2.GND#6
  N5: NEOPIXEL1.Din, NEOPIXEL2.Dout
  N6: NEOPIXEL1.+5V#3, NEOPIXEL2.+5V#4
  N7: NEOPIXEL2.GND#1, NEOPIXEL5.GND#6
  N8: NEOPIXEL2.Din, NEOPIXEL5.Dout
  N9: NEOPIXEL2.+5V#3, NEOPIXEL5.+5V#4
  N10: NEOPIXEL3.GND, NEOPIXEL4.GND#6
  N11: NEOPIXEL3.Din, NEOPIXEL4.Dout
  N12: NEOPIXEL3.+5V, NEOPIXEL4.+5V#4
  N13: NEOPIXEL4.GND#1, NEOPIXEL5.GND#1
  N14: NEOPIXEL4.Din, NEOPIXEL5.Din
  N15: NEOPIXEL4.+5V#3, NEOPIXEL5.+5V#3

custom parts:
  Neopixel Strip -- Black (30/m): These NeoPixel strips have 30 digitally-addressable pixel LEDs per meter and are very affordable and are only 12.5 mm wide, 10 mm if you remove the strip from the casing.
