# Fritzing sketch Spooky Eyes_without_sensor (saved by Fritzing 0.9.3b)

parts:
  Part1 = Arduino Uno (Rev3)
  NEOPIXEL1 = Neopixel Strip -- Black (30/m)
  Power_plug1 = Power plug  # not connected
  NEOPIXEL2 = Neopixel Strip -- Black (30/m)
  NEOPIXEL3 = Neopixel Strip -- Black (30/m)
  NEOPIXEL4 = Neopixel Strip -- Black (30/m)
  NEOPIXEL5 = Neopixel Strip -- Black (30/m)

nets:
  N1: Part1.D6_PWM, NEOPIXEL1.Dout
  N2: NEOPIXEL1.GND#1, NEOPIXEL2.GND#6
  N3: NEOPIXEL1.Din, NEOPIXEL2.Dout
  N4: NEOPIXEL1.+5V#3, NEOPIXEL2.+5V#4
  N5: NEOPIXEL2.GND#1, NEOPIXEL5.GND#6
  N6: NEOPIXEL2.Din, NEOPIXEL5.Dout
  N7: NEOPIXEL2.+5V#3, NEOPIXEL5.+5V#4
  N8: NEOPIXEL3.GND, NEOPIXEL4.GND#6
  N9: NEOPIXEL3.Din, NEOPIXEL4.Dout
  N10: NEOPIXEL3.+5V, NEOPIXEL4.+5V#4
  N11: NEOPIXEL4.GND#1, NEOPIXEL5.GND#1
  N12: NEOPIXEL4.Din, NEOPIXEL5.Din
  N13: NEOPIXEL4.+5V#3, NEOPIXEL5.+5V#3

custom parts:
  Neopixel Strip -- Black (30/m): These NeoPixel strips have 30 digitally-addressable pixel LEDs per meter and are very affordable and are only 12.5 mm wide, 10 mm if you remove the strip from the casing.
